# Fritzing sketch switch (saved by Fritzing 0.9.3b)
perfboards: 1

parts:
  AC = Header 2 [package=screwterminal-3.5mm-2_lock]  # not connected
  R1 = Resistor [tolerance=±5% resistance=220 package=THT]
  R2 = Resistor [tolerance=±5% resistance=360 package=THT]
  Cin = Electrolytic Capacitor [capacitance=1µF package="100 mil [THT, electrolytic]"]
  Cout = Electrolytic Capacitor [capacitance=1µF package="100 mil [THT, electrolytic]"]
  5VDC = Header 1 [package=1x01_offset]
  GND = Header 1 [package=1x01_offset]
  U1 = Voltage Regulator - Variable [package="TO220 [THT]"]

nets:
  N1: R1.Pin_0, Cout.+, U1.OUT
  N2: R1.Pin_1, R2.Pin_0, U1.ADJ
  GND: R2.Pin_1, Cin.-, Cout.-, GND.1
  N3: Cin.+, 5VDC.1, U1.IN
